// Logisim project partial-load.circ as structural Verilog: 1 circuit, main circuit partial_load
module partial_load (
  input  [31:0] Instruction,
  input  [31:0] MemAddress,
  input  [31:0] DataFromMem,
  output [31:0] DataToReg
);

  wire [1:0] funct3;
  wire [31:0] undriven;

  Multiplexer #(.select(2), .width(32)) multiplexer_1 (
    .in1(undriven), .in2(DataFromMem), .sel(funct3));  // open: in0, in3, out

  // Notes on the sheet:
  //   INPUTS to your circuit
  //   DON'T CHANGE THE LOCATIONS OF THE INPUTS AND OUTPUTS!
  //   OUTPUT from your circuit
endmodule
