// Logisim project regfile.circ as structural Verilog: 1 circuit, main circuit regfile
module regfile (
  input  [4:0] ReadIndex1,
  input  [4:0] ReadIndex2,
  input  [4:0] WriteIndex,
  input  [31:0] WriteData,
  input  RegWEn,
  input  clk,
  output [31:0] ra,
  output [31:0] sp,
  output [31:0] t0,
  output [31:0] t1,
  output [31:0] t2,
  output [31:0] s0,
  output [31:0] s1,
  output [31:0] a0,
  output [31:0] ReadData1,
  output [31:0] ReadData2
);

  wire WEn_ra;
  wire [1:0] demultiplexer_1_p3, demultiplexer_1_p4, demultiplexer_1_p5, demultiplexer_1_p6,
       demultiplexer_1_p7, WEn_a0;

  // Demultiplexer #(.select(5)) demultiplexer_1: pin names not known; wires that end beside it: RegWEn, WriteIndex, demultiplexer_1_p3, demultiplexer_1_p4, demultiplexer_1_p5, demultiplexer_1_p6, demultiplexer_1_p7, WEn_a0
  Register #(.width(32)) register_1 (.D(WriteData), .en(WEn_ra), .clk(clk), .Q(ra));  // open: clr
  Register #(.width(32)) register_2 (.D(WriteData), .en(RegWEn), .clk(clk), .Q(sp));  // open: clr
  Register #(.width(32)) register_3 (.D(WriteData), .en(RegWEn), .clk(clk), .Q(t0));  // open: clr
  Register #(.width(32)) register_4 (.D(WriteData), .en(RegWEn), .clk(clk), .Q(t1));  // open: clr
  Register #(.width(32)) register_5 (.D(WriteData), .en(RegWEn), .clk(clk), .Q(t2));  // open: clr
  Register #(.width(32)) register_6 (.D(WriteData), .en(RegWEn), .clk(clk), .Q(s0));  // open: clr
  Register #(.width(32)) register_7 (.D(WriteData), .en(RegWEn), .clk(clk), .Q(s1));  // open: clr
  Register #(.width(32)) register_8 (.D(WriteData), .en(RegWEn), .clk(clk), .Q(a0));  // open: clr

  // Notes on the sheet:
  //   INPUTS to your circuit
  //   DON'T CHANGE THE LOCATIONS OF THE INPUTS AND OUTPUTS!
  //   These are DEBUG/TEST outputs from your circuit.
  //   OUTPUTS from your circuit
endmodule
